# Fritzing sketch 28BYJ (saved by Fritzing 0.9.3b)

parts:
  Mod1 = Raspberry Pi Pico
  SM1 = 28BYJ-48 Stepper Motor [part_number=28BYJ-48]
  Driver1 = 28BYJ-48 Driver Module [part_number=ULN2003 package=THT]

nets:
  N1: Mod1.pin_1, Driver1.IN1
  N2: Mod1.pin_2, Driver1.IN2
  N3: Mod1.pin_4, Driver1.IN3
  N4: Mod1.pin_5, Driver1.IN4
  N5: Mod1.pin_38, Mod1.pin_42, Driver1.GND
  N6: Mod1.pin_40, Driver1.Vmotor
  N7: SM1.blue-pin, Driver1.blue-pin
  N8: SM1.pink-pin, Driver1.pink-pin
  N9: SM1.yellow-pin, Driver1.yellow-pin
  N10: SM1.orange-pin, Driver1.orange-pin
  N11: SM1.red-pin, Driver1.red-pin

custom parts:
  Raspberry Pi Pico: Raspberry Pi Pico. Based around the RP2040 microcontroller the Pico is a low cost microcontroller device bringing Raspberry Pi quality, cost, and easy of use to the microcontroller space. Jan 2021, Split part in to two versions: tht (this one) and SMD. This one will drill holes for a .1 in header in pcb to allow plugging in the module as well as providing pads to solder the module to the top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
  28BYJ-48 Stepper Motor: Unipolar Stepper Motor 28BYJ-48 Top coil - pink & orange Bottom coil - blue & yellow Common rail - red Connector pins: blue - pink - yellow - orange - red
  28BYJ-48 Driver Module: High-power ULN2003 Stepper Motor Driver Board Test Module For Arduino AVR SMD
