# Fritzing sketch DCmotor (saved by Fritzing 0.9.3b)
circuit board: 8.46667cm x 5.64444cm
breadboards: 1

parts:
  BC547B = NPN-Transistor [package="TO92 [THT]"]
  Mod1 = Raspberry Pi Pico
  D1 = Rectifier Diode [part_number=1N4001 package="300 mil [THT]"]
  R1 = Resistor [tolerance=±5% resistance=220 package=THT]
  M1 = DC Motor

nets:
  N1: BC547B.E, D1.anode, M1.pin_1
  N2: BC547B.B, R1.Pin_0
  N3: BC547B.C, Mod1.pin_3, Mod1.pin_8, Mod1.pin_23
  N4: Mod1.pin_26, R1.Pin_1
  N5: Mod1.pin_40, D1.cathode, M1.pin_2

custom parts:
  Raspberry Pi Pico: Raspberry Pi Pico. Based around the RP2040 microcontroller the Pico is a low cost microcontroller device bringing Raspberry Pi quality, cost, and easy of use to the microcontroller space. Jan 2021, Split part in to two versions: tht (this one) and SMD. This one will drill holes for a .1 in header in pcb to allow plugging in the module as well as providing pads to solder the module to the top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
